// Logisim project misc16bit.circ as structural Verilog: 3 circuits, main circuit main
module main (
  input  in_1
);

  wire and_1_out, button_1_out, data_flag, data_instr_out, demultiplexer_1_out5, execute, fetch, inc_IAR,
       multiplexer_2_out, write;
  wire [2:0] counter_1_q;
  wire [15:0] adder_1_out, D_q, demultiplexer_2_out0, demultiplexer_2_out1, IAR_q, instr, JAR_q, KR_q, MAR_q,
       multiplexer_1_out, pull_resistor_1_node, R0_q, R1_q, R2_q, ram_1_dout, rom_1_data;

  Pull_Resistor pull_resistor_1 (.node(pull_resistor_1_node));
  Register #(.width(16)) MAR (.D(pull_resistor_1_node), .Q(MAR_q));  // open: en, clk, clr
  // Probe on pull_resistor_1_node
  Counter #(.max('h7), .width(3)) counter_1 (
    .Q(counter_1_q), .clk(button_1_out), .clr(demultiplexer_1_out5));  // open: load, D, count, carry, up
  Button button_1 (.out(button_1_out));
  ROM #(.addrWidth(16), .dataWidth(16)) rom_1 (.addr(IAR_q), .data(rom_1_data));
  RAM #(.addrWidth(16), .dataWidth(16), .trigger("high")) ram_1 (.addr(MAR_q), .dout(ram_1_dout));  // open: we, oe, din
  Controlled_Buffer #(.width(16)) controlled_buffer_1 (.in(MAR_q), .out(pull_resistor_1_node));  // open: en
  Demultiplexer #(.select(3)) demultiplexer_1 (
    .out1(fetch), .out2(execute), .out3(write), .out4(inc_IAR), .out5(demultiplexer_1_out5), .in(1'b1),
    .sel(counter_1_q));  // open: out0, out6, out7
  Adder #(.width(16)) adder_1 (.a(16'h1), .b(IAR_q), .out(adder_1_out));  // open: cin, cout
  Multiplexer #(.width(16)) multiplexer_1 (.in0(adder_1_out), .in1(JAR_q), .out(multiplexer_1_out), .sel(in_1));
  Register #(.width(16)) IAR (.D(multiplexer_1_out), .clk(inc_IAR), .Q(IAR_q));  // open: en, clr
  Controlled_Buffer #(.width(16)) controlled_buffer_2 (.in(IAR_q), .out(pull_resistor_1_node));  // open: en
  Demultiplexer #(.width(16)) demultiplexer_2 (
    .out0(demultiplexer_2_out0), .out1(demultiplexer_2_out1), .in(rom_1_data), .sel(data_flag));
  Register #(.width(16)) D (.D(demultiplexer_2_out1), .clk(and_1_out), .Q(D_q));  // open: en, clr
  Controlled_Buffer #(.width(16)) controlled_buffer_3 (.in(D_q), .out(pull_resistor_1_node));  // open: en
  and and_1 (and_1_out, fetch, data_flag);
  Register #(.width(16)) R0 (.D(pull_resistor_1_node), .Q(R0_q));  // open: en, clk, clr
  Controlled_Buffer #(.width(16)) controlled_buffer_4 (.in(R0_q), .out(pull_resistor_1_node));  // open: en
  Register #(.width(16)) IR (.D(demultiplexer_2_out0), .clk(fetch), .Q(instr));  // open: en, clr
  Register #(.width(16)) R1 (.D(pull_resistor_1_node), .Q(R1_q));  // open: en, clk, clr
  Controlled_Buffer #(.width(16)) controlled_buffer_5 (.in(R1_q), .out(pull_resistor_1_node));  // open: en
  Register #(.width(16)) R2 (.D(pull_resistor_1_node), .Q(R2_q));  // open: en, clk, clr
  Controlled_Buffer #(.width(16)) controlled_buffer_6 (.in(R2_q), .out(pull_resistor_1_node));  // open: en
  and data_instr (data_instr_out, instr[12], ~instr[13], ~instr[14], ~instr[15]);  // AND_Gate
  Register #(.width(16)) JAR (.D(pull_resistor_1_node), .Q(JAR_q));  // open: en, clk, clr
  Multiplexer multiplexer_2 (.in0(data_instr_out), .in1(1'b0), .out(multiplexer_2_out), .sel(data_flag));
  alu alu_1 (.opcode(instr[15:12]));  // open: x, y, o
  D_Flip_Flop d_ff_1 (.D(multiplexer_2_out), .clk(execute), .Q(data_flag));  // open: Qn, preset, reset
  Register #(.width(16)) KR (.D(pull_resistor_1_node), .Q(KR_q));  // open: en, clk, clr
  Controlled_Buffer #(.width(16)) controlled_buffer_7 (.in(KR_q), .out(pull_resistor_1_node));  // open: en
  Controlled_Buffer #(.width(16)) controlled_buffer_8 (.in(ram_1_dout), .out(pull_resistor_1_node));  // open: en
  control_unit control_unit_1 (.instr(instr));  // open: e_D, e_R0, e_R1, e_R2

  // Notes on the sheet:
  //   contents of rom_1 (hex, n*v repeats v):
  //   1000 5 2000
  //   Эта общая шина нужна для того чтобы реализовать команду move
endmodule

module control_unit (
  input  [15:0] instr,
  output e_D,
  output e_R0,
  output e_R1,
  output e_R2
);

  wire MOVE_out;

  and MOVE (MOVE_out, ~instr[15], ~instr[14], instr[13], ~instr[12]);  // AND_Gate
endmodule

module alu (
  input  [15:0] x,
  input  [15:0] y,
  input  [3:0] opcode,
  output [15:0] o
);

  wire [15:0] adder_1_out, and_1_out, not_1_out, or_1_out, subtractor_1_out;

  Adder #(.width(16)) adder_1 (.a(x), .b(y), .out(adder_1_out));  // open: cin, cout
  Subtractor #(.width(16)) subtractor_1 (.a(x), .b(y), .out(subtractor_1_out));  // open: bin, bout
  assign and_1_out = x & y;  // AND_Gate and_1, 16 bits wide
  assign or_1_out = x | y;  // OR_Gate or_1, 16 bits wide
  assign not_1_out = ~x;  // NOT_Gate not_1, 16 bits wide
  Multiplexer #(.select(4), .width(16)) multiplexer_1 (
    .in3(adder_1_out), .in4(subtractor_1_out), .in5(and_1_out), .in6(or_1_out), .in7(not_1_out), .out(o),
    .sel(opcode));  // open: in0, in1, in2, in8, in9, in10, in11, in12, in13, in14, in15
endmodule
